// Logisim project 4 BİTLİK ÇIKARMAYI TAM ÇIKARICI İLE YAPMA.circ as structural Verilog: 1 circuit, main circuit main
module main (
  input  A0,
  input  A1,
  input  A2,
  input  A3,
  input  B0,
  input  B1,
  input  B2,
  input  B3,
  input  BG,
  output F0,
  output F1,
  output F2,
  output F3,
  output B
);

  wire and_1_out, and_2_out, and_3_out, and_4_out, and_5_out, and_6_out, and_7_out, and_8_out, and_9_out,
       and_10_out, and_11_out, and_12_out, not_1_out, not_2_out, not_3_out, not_4_out, or_1_out, or_2_out,
       or_3_out, xor_1_out, xor_3_out, xor_5_out, xor_7_out;

  xor xor_1 (xor_1_out, A0, B0);
  not not_1 (not_1_out, A0);
  xor xor_2 (F0, xor_1_out, BG);
  and and_1 (and_1_out, not_1_out, B0);
  and and_2 (and_2_out, not_1_out, BG);
  and and_3 (and_3_out, B0, BG);
  or or_1 (or_1_out, and_1_out, and_2_out, and_3_out);
  xor xor_3 (xor_3_out, A1, B1);
  not not_2 (not_2_out, A1);
  xor xor_4 (F1, xor_3_out, or_1_out);
  and and_4 (and_4_out, not_2_out, B1);
  and and_5 (and_5_out, not_2_out, or_1_out);
  and and_6 (and_6_out, B1, or_1_out);
  or or_2 (or_2_out, and_4_out, and_5_out, and_6_out);
  not not_3 (not_3_out, A2);
  xor xor_5 (xor_5_out, A2, B2);
  and and_7 (and_7_out, not_3_out, B2);
  and and_8 (and_8_out, not_3_out, or_2_out);
  and and_9 (and_9_out, B2, or_2_out);
  xor xor_6 (F2, xor_5_out, or_2_out);
  or or_3 (or_3_out, and_7_out, and_8_out, and_9_out);
  xor xor_7 (xor_7_out, A3, B3);
  not not_4 (not_4_out, A3);
  and and_10 (and_10_out, not_4_out, B3);
  and and_11 (and_11_out, not_4_out, or_3_out);
  and and_12 (and_12_out, B3, or_3_out);
  xor xor_8 (F3, xor_7_out, or_3_out);
  or or_4 (B, and_10_out, and_11_out, and_12_out);

  // Notes on the sheet:
  //   2 BİTLİK ÇIKARMAYI TAM ÇIKARICI İLE YAPMA
endmodule
