// Logisim project 4X1 MUX ÖDEV SORUSU.circ as structural Verilog: 1 circuit, main circuit main
module main (
  input  X1,
  input  X2,
  input  X3,
  input  X4,
  output out_5
);

  wire and_1_out, and_2_out, and_3_out, and_4_out, and_5_out, and_6_out, not_1_out, not_2_out, not_3_out,
       not_4_out, or_1_out, xor_1_out;

  not not_1 (not_1_out, X1);
  not not_2 (not_2_out, X2);
  xor xor_1 (xor_1_out, X1, X2);
  and and_1 (and_1_out, not_1_out, not_2_out);
  and and_2 (and_2_out, X1, not_2_out);
  or or_1 (or_1_out, and_1_out, xor_1_out);
  not not_3 (not_3_out, X4);
  not not_4 (not_4_out, X3);
  and and_3 (and_3_out, and_2_out, not_3_out, not_4_out);
  and and_4 (and_4_out, xor_1_out, not_4_out, X4);
  and and_5 (and_5_out, not_2_out, X3, not_3_out);
  and and_6 (and_6_out, or_1_out, X3, X4);
  or or_2 (out_5, and_3_out, and_4_out, and_5_out, and_6_out);

  // Notes on the sheet:
  //   4X1 MUX ÖDEV SORUSU
endmodule
