// Logisim project KOMBİNOZANSAL DEVRE TASARIMI.circ as structural Verilog: 1 circuit, main circuit main
module main (
  input  X1,
  input  X1_2,
  input  X2,
  input  X2_2,
  input  X1_3,
  input  X1_4,
  input  X2_3,
  input  X2_4,
  output out_9,
  output out_10,
  output out_11,
  output out_12
);

  wire and_1_out, and_2_out, nand_1_out, nand_2_out, nand_3_out, nand_4_out, nand_5_out, nand_6_out,
       nand_7_out, nand_8_out, nor_1_out, nor_2_out, nor_3_out, nor_4_out, nor_5_out, nor_6_out, nor_7_out,
       nor_8_out, nor_9_out, not_1_out, not_2_out;

  not not_1 (not_1_out, X1_2);
  not not_2 (not_2_out, X2_2);
  nand nand_1 (nand_1_out, X1_4, X1_4);
  nand nand_2 (nand_2_out, X2_4, X2_4);
  nand nand_3 (nand_3_out, X1_4, X2_4);
  and and_1 (and_1_out, not_1_out, not_2_out);
  and and_2 (and_2_out, X1_2, X2_2);
  nand nand_4 (nand_4_out, nand_1_out, nand_2_out);
  nand nand_5 (nand_5_out, nand_3_out, nand_3_out);
  nand nand_6 (nand_6_out, nand_4_out, nand_4_out);
  or or_1 (out_10, and_1_out, and_2_out);
  nand nand_7 (nand_7_out, nand_6_out, nand_6_out);
  nand nand_8 (nand_8_out, nand_5_out, nand_5_out);
  nand nand_9 (out_11, nand_7_out, nand_8_out);
  nor nor_1 (nor_1_out, X1_3, X1_3);
  nor nor_2 (nor_2_out, X2_3, X2_3);
  xnor xnor_1 (out_9, X1, X2);
  nor nor_3 (nor_3_out, nor_1_out, nor_1_out);
  nor nor_4 (nor_4_out, nor_2_out, nor_2_out);
  nor nor_5 (nor_5_out, X1_3, X1_3);
  nor nor_6 (nor_6_out, X2_3, X2_3);
  nor nor_7 (nor_7_out, nor_5_out, nor_6_out);
  nor nor_8 (nor_8_out, nor_3_out, nor_4_out);
  nor nor_9 (nor_9_out, nor_8_out, nor_7_out);
  nor nor_10 (out_12, nor_9_out, nor_9_out);

  // Notes on the sheet:
  //   KOMBİNOZANSAL DEVRE TASARIMI
  //   Y=X1'X2'+X1X2
  //   NAND İLE YAPILIŞ
  //   XNOR İLE YAPILIŞ
  //   NOR İLE YAPILIŞ
endmodule
