// Logisim project NORMAL TAM TOPLAYICI.circ as structural Verilog: 1 circuit, main circuit main
module main (
  input  EG,
  input  A,
  input  B,
  output T,
  output E
);

  wire and_1_out, and_2_out, or_1_out, xor_1_out;

  xor xor_1 (xor_1_out, A, B);
  or or_1 (or_1_out, A, B);
  and and_1 (and_1_out, A, B);
  xor xor_2 (T, EG, xor_1_out);
  and and_2 (and_2_out, EG, or_1_out);
  or or_2 (E, and_2_out, and_1_out);

  // Notes on the sheet:
  //   NORMAL TAM TOPLAYICI
endmodule
