// Logisim project TAM TOPLAYICIYLA ALT FONKSİYONLAR.circ as structural Verilog: 1 circuit, main circuit main
module main (
  input  EG0,
  input  A3,
  input  A0,
  input  B3,
  input  B0,
  input  A1,
  input  A2,
  input  B1,
  input  B2,
  output T3,
  output T0,
  output E4,
  output T1,
  output T2
);

  wire and_1_out, and_2_out, and_3_out, and_4_out, and_5_out, and_6_out, and_7_out, and_8_out, or_1_out,
       or_2_out, or_3_out, or_4_out, or_5_out, or_6_out, or_7_out, xor_1_out, xor_2_out, xor_5_out, xor_7_out;

  and and_1 (and_1_out, A0, B0);
  and and_2 (and_2_out, A1, B1);
  xor xor_1 (xor_1_out, A0, B0);
  or or_1 (or_1_out, A0, B0);
  xor xor_2 (xor_2_out, A1, B1);
  or or_2 (or_2_out, A1, B1);
  and and_3 (and_3_out, EG0, or_1_out);
  or or_3 (or_3_out, and_3_out, and_1_out);
  and and_4 (and_4_out, or_3_out, or_2_out);
  xor xor_3 (T0, EG0, xor_1_out);
  xor xor_4 (T1, or_3_out, xor_2_out);
  or or_4 (or_4_out, and_4_out, and_2_out);
  xor xor_5 (xor_5_out, A2, B2);
  or or_5 (or_5_out, A2, B2);
  and and_5 (and_5_out, A2, B2);
  and and_6 (and_6_out, or_4_out, or_5_out);
  xor xor_6 (T2, or_4_out, xor_5_out);
  or or_6 (or_6_out, and_6_out, and_5_out);
  and and_7 (and_7_out, A3, B3);
  xor xor_7 (xor_7_out, A3, B3);
  or or_7 (or_7_out, A3, B3);
  and and_8 (and_8_out, or_6_out, or_7_out);
  or or_8 (E4, and_8_out, and_7_out);
  xor xor_8 (T3, or_6_out, xor_7_out);

  // Notes on the sheet:
  //   EG1
  //   TAM TOPLAYICIYLA ALT FONKSİYONLAR
  //   EG1
  //   EG2
  //   EG2
  //   EG3
  //   EG3
endmodule
