// Logisim project TAM ÇIKARICI.circ as structural Verilog: 1 circuit, main circuit main
module main (
  input  A,
  input  A_2,
  input  B,
  input  B_2,
  input  BG,
  input  BG_2,
  output F,
  output F_2,
  output B_3,
  output B_4
);

  wire and_1_out, and_2_out, and_3_out, and_4_out, and_5_out, and_6_out, and_7_out, and_8_out, and_9_out,
       and_10_out, not_1_out, not_2_out, not_3_out, not_4_out, xor_1_out;

  xor xor_1 (xor_1_out, A_2, B);
  not not_1 (not_1_out, A_2);
  xor xor_2 (F_2, xor_1_out, BG);
  and and_1 (and_1_out, not_1_out, B);
  and and_2 (and_2_out, not_1_out, BG);
  and and_3 (and_3_out, B, BG);
  or or_1 (B_3, and_1_out, and_2_out, and_3_out);
  not not_2 (not_2_out, A);
  not not_3 (not_3_out, B_2);
  not not_4 (not_4_out, BG_2);
  and and_4 (and_4_out, not_2_out, not_3_out, BG_2);
  and and_5 (and_5_out, not_2_out, B_2, not_4_out);
  and and_6 (and_6_out, A, not_3_out, not_4_out);
  and and_7 (and_7_out, A, B_2, BG_2);
  and and_8 (and_8_out, not_2_out, B_2);
  and and_9 (and_9_out, not_2_out, BG_2);
  and and_10 (and_10_out, B_2, BG_2);
  or or_2 (B_4, and_8_out, and_9_out, and_10_out);
  or or_3 (F, and_4_out, and_5_out, and_6_out, and_7_out);

  // Notes on the sheet:
  //   TAM ÇIKARICI
endmodule
