// Logisim project TAMAMMLANMIŞ ÖDEV1 LOJİK.circ as structural Verilog: 1 circuit, main circuit main
module main (
  input  A1,
  input  A0,
  input  B1,
  input  B0,
  output T0,
  output T1,
  output T2
);

  wire A0_prime_out, A1_prime_out, and_1_out, and_2_out, and_3_out, and_4_out, and_5_out, and_6_out,
       and_7_out, and_8_out, and_9_out, and_10_out, B0_prime_out, B1_prime_out;

  not A1_prime (A1_prime_out, A1);
  not A0_prime (A0_prime_out, A0);
  not B1_prime (B1_prime_out, B1);
  not B0_prime (B0_prime_out, B0);
  and and_1 (and_1_out, A1_prime_out, B1);
  and and_2 (and_2_out, A1_prime_out, A0_prime_out, B0);
  and and_3 (and_3_out, A0_prime_out, B0, B1);
  and and_4 (and_4_out, A1_prime_out, A0_prime_out, B1_prime_out, B0_prime_out);
  and and_5 (and_5_out, A1_prime_out, A0, B1_prime_out, B0);
  and and_6 (and_6_out, A1, A0, B1, B0);
  and and_7 (and_7_out, A1, A0_prime_out, B1, B0_prime_out);
  and and_8 (and_8_out, A1, B1_prime_out);
  and and_9 (and_9_out, A0, B1_prime_out, B0_prime_out);
  and and_10 (and_10_out, A1, A0, B0_prime_out);
  or or_1 (T0, and_1_out, and_2_out, and_3_out);
  or or_2 (T1, and_4_out, and_5_out, and_6_out, and_7_out);
  or or_3 (T2, and_8_out, and_9_out, and_10_out);

  // Notes on the sheet:
  //   T0=A1'B1+A1'A0'B0+A0'B0B1
  //   T2=A1B1'+A0B1'B0'+A1A0B0'
  //   T1=A1'A0'B1'B0'+A1'A0B1'B0+A1A0B1B0+A1A0'B1B0'
endmodule
