// Logisim project TOPLAMLAR ÇARPIMI NOR.circ as structural Verilog: 1 circuit, main circuit main
module main (
  input  A,
  input  B,
  input  C,
  output out_4
);

  wire nor_1_out, nor_2_out, nor_3_out;

  nor nor_1 (nor_1_out, A, A);
  nor nor_2 (nor_2_out, A, B);
  nor nor_3 (nor_3_out, nor_1_out, C);
  nor nor_4 (out_4, nor_3_out, nor_2_out);

  // Notes on the sheet:
  //   F=[A+B][A'+C]
endmodule
