// Logisim project Türetilmiş kapılarla temel lojik kapıların yapılması.circ as structural Verilog: 1 circuit, main circuit main
module main (
  input  A,
  input  A_2,
  input  A_3,
  input  B,
  input  A_4,
  input  A_5,
  input  B_2,
  input  A_6,
  input  A_7,
  input  B_3,
  input  B_4,
  output \TÜMLEME_NOT ,
  output out_13,
  output out_14,
  output out_15,
  output out_16,
  output out_17,
  output out_18
);

  wire nand_2_out, nand_3_out, nand_5_out, nor_2_out, nor_5_out, nor_6_out;

  // NOT_Gate not_1 is placed but not wired
  not not_2 (\TÜMLEME_NOT , A);
  nand nand_1 (out_15, A_4, A_4);
  nand nand_2 (nand_2_out, A_6, A_6);
  nand nand_3 (nand_3_out, B_4, B_4);
  // AND_Gate and_1 is placed but not wired
  nand nand_4 (out_18, nand_2_out, nand_3_out);
  // OR_Gate or_1 is placed but not wired
  nor nor_1 (out_16, A_5, A_5);
  nor nor_2 (nor_2_out, A_7, B_3);
  nand nand_5 (nand_5_out, A_3, B);
  nor nor_3 (out_17, nor_2_out, nor_2_out);
  // NAND_Gate nand_6 is placed but not wired
  nand nand_7 (out_13, nand_5_out, nand_5_out);
  // NOR_Gate nor_4 is placed but not wired
  // XOR_Gate xor_1 is placed but not wired
  nor nor_5 (nor_5_out, A_2, A_2);
  nor nor_6 (nor_6_out, B_2, B_2);
  // XNOR_Gate xnor_1 is placed but not wired
  nor nor_7 (out_14, nor_5_out, nor_6_out);

  // Notes on the sheet:
  //   NOT
  //   NAND
  //   NAND
  //   TEMEL LOJİK KAPILARI
  //   AND
  //   OR(VEYA)
  //   F=A+B
  //   OR
  //   NOR
  //   NOR
  //   NAND
  //   NAND
  //   AND(VE)
  //   TÜRETİLMİŞ KAPILAR
  //   NOR
  //   F=AB
  //   XOR
  //   XNOR
  //   NOR
endmodule
