// Logisim project YARI TOPLAYICI.circ as structural Verilog: 1 circuit, main circuit main
module main (
  input  A,
  input  B,
  input  A_2,
  input  B_2,
  output T,
  output E
);

  wire and_2_out, xor_2_out;

  xor xor_1 (T, A, B);
  and and_1 (E, A, B);
  xor xor_2 (xor_2_out, A_2, B_2);
  and and_2 (and_2_out, A_2, B_2);
  LED led_1 (.in(xor_2_out));
  LED led_2 (.in(and_2_out));

  // Notes on the sheet:
  //   YARI TOPLAYICI
  //   YARI TOPLAYICI
endmodule
