// Logisim project YARI TOPLAYICIDAN TAM TOPLAYICI.circ as structural Verilog: 1 circuit, main circuit main
module main (
  input  EG,
  input  A,
  input  B,
  output T1,
  output EG_2
);

  wire and_1_out, and_2_out, xor_1_out;

  xor xor_1 (xor_1_out, A, B);
  and and_1 (and_1_out, A, B);
  xor xor_2 (T1, EG, xor_1_out);
  and and_2 (and_2_out, EG, xor_1_out);
  or or_1 (EG_2, and_2_out, and_1_out);

  // Notes on the sheet:
  //   T0
  //   E0
  //   YARI TOPLAYICIDAN TAM TOPLAYICI
  //   E1
endmodule
