// Logisim project YARI ÇIKARICI.circ as structural Verilog: 1 circuit, main circuit main
module main (
  input  A,
  input  B,
  output F,
  output B_2
);

  wire not_1_out;

  not not_1 (not_1_out, A);
  xor xor_1 (F, A, B);
  and and_1 (B_2, not_1_out, B);

  // Notes on the sheet:
  //   YARI ÇIKARICI
endmodule
