// Logisim project lojik_örnek1.circ as structural Verilog: 2 circuits, main circuit main
module main (
  input  A,
  input  A_2,
  input  B,
  input  B_2,
  input  C,
  input  C_2,
  input  A_3,
  input  B_3,
  input  C_3,
  output Y,
  output out_11,
  output out_12
);

  wire and_1_out, and_2_out, and_3_out, and_4_out, and_5_out, and_6_out, and_7_out, and_8_out, not_1_out,
       not_2_out, not_3_out, not_4_out, not_5_out;

  not not_1 (not_1_out, A_2);
  not not_2 (not_2_out, A_3);
  not not_3 (not_3_out, B_3);
  not not_4 (not_4_out, C_3);
  and and_1 (and_1_out, A_2, B);
  and and_2 (and_2_out, not_1_out, C_2);
  and and_3 (and_3_out, not_2_out, not_3_out, C_3);
  and and_4 (and_4_out, not_2_out, B_3, C_3);
  and and_5 (and_5_out, not_4_out, A_3, B_3);
  and and_6 (and_6_out, A_3, B_3, C_3);
  or or_1 (out_11, and_1_out, and_2_out);
  or or_2 (out_12, and_3_out, and_4_out, and_5_out, and_6_out);
  not not_5 (not_5_out, A);
  and and_7 (and_7_out, not_5_out, C);
  and and_8 (and_8_out, A, B_2);
  or or_3 (Y, and_7_out, and_8_out);

  // Notes on the sheet:
  //   F=AB+A'C
  //   AYNISI
  //   F=A'B'C+A'BC+ABC'+ABC
endmodule

module \örnek1  (
  input  A,
  input  B,
  input  C,
  output Y
);

  wire and_1_out, and_2_out, not_1_out;

  not not_1 (not_1_out, A);
  and and_1 (and_1_out, not_1_out, C);
  and and_2 (and_2_out, A, B);
  or or_1 (Y, and_1_out, and_2_out);
endmodule
