// Logisim project ÇARPIMLAR TOPLAMI NAND TASARIMI.circ as structural Verilog: 1 circuit, main circuit main
module main (
  input  A,
  input  B,
  input  C,
  output out_4
);

  wire nand_1_out, nand_2_out, nand_3_out;

  nand nand_1 (nand_1_out, A, A);
  nand nand_2 (nand_2_out, nand_1_out, C);
  nand nand_3 (nand_3_out, A, B);
  nand nand_4 (out_4, nand_2_out, nand_3_out);

  // Notes on the sheet:
  //   F=A'C+AB
endmodule
