// Logisim project ÇARPIMLAR TOPLAMI NOR TASARIMI.circ as structural Verilog: 1 circuit, main circuit main
module main (
  input  A,
  input  B,
  input  C,
  output out_4
);

  wire nor_1_out, nor_2_out, nor_3_out, nor_4_out, nor_5_out, nor_6_out;

  nor nor_1 (nor_1_out, C, C);
  nor nor_2 (nor_2_out, A, nor_1_out);
  nor nor_3 (nor_3_out, A, A);
  nor nor_4 (nor_4_out, B, B);
  nor nor_5 (nor_5_out, nor_3_out, nor_4_out);
  nor nor_6 (nor_6_out, nor_2_out, nor_5_out);
  nor nor_7 (out_4, nor_6_out, nor_6_out);

  // Notes on the sheet:
  //   F=A'C+AB
endmodule
