// Logisim project örnek2.circ as structural Verilog: 1 circuit, main circuit main
module main (
  input  A,
  input  A_2,
  input  B,
  input  B_2,
  input  C,
  input  C_2,
  input  D,
  input  D_2,
  input  A_3,
  input  B_3,
  input  C_3,
  input  D_3,
  output out_13,
  output out_14,
  output out_15
);

  wire and_1_out, and_2_out, and_3_out, and_4_out, and_5_out, and_6_out, and_7_out, and_8_out, not_1_out,
       not_2_out, not_3_out, not_4_out, not_5_out, not_6_out;

  not not_1 (not_1_out, C_2);
  not not_2 (not_2_out, B_2);
  and and_1 (and_1_out, C_2, D_2);
  and and_2 (and_2_out, B_2, not_1_out);
  and and_3 (and_3_out, A_2, not_2_out, D_2);
  or or_1 (out_14, and_1_out, and_2_out, and_3_out);
  not not_3 (not_3_out, C);
  not not_4 (not_4_out, A);
  not not_5 (not_5_out, D);
  not not_6 (not_6_out, C_3);
  and and_4 (and_4_out, B, not_3_out, not_5_out);
  and and_5 (and_5_out, A_3, D_3);
  and and_6 (and_6_out, B_3, not_6_out);
  and and_7 (and_7_out, A, D);
  and and_8 (and_8_out, not_3_out, not_4_out, B);
  or or_2 (out_15, and_5_out, and_6_out);
  or or_3 (out_13, and_7_out, and_8_out, and_4_out);

  // Notes on the sheet:
  //   F=BC'+ACD+AB'D
  //   F=AD+BC'
  //   F=AD+A'BC'+BC'D'
endmodule
