// Logisim project örnek3.circ as structural Verilog: 1 circuit, main circuit main
module main (
  input  A,
  input  B,
  input  C,
  input  D,
  output out_5
);

  wire and_1_out, and_2_out, and_3_out, not_1_out, not_2_out, not_3_out;

  not not_1 (not_1_out, B);
  not not_2 (not_2_out, C);
  and and_1 (and_1_out, not_1_out, not_2_out, D);
  and and_2 (and_2_out, B, C, D);
  not not_3 (not_3_out, D);
  and and_3 (and_3_out, A, B, not_3_out);
  or or_1 (out_5, and_3_out, and_1_out, and_2_out);

  // Notes on the sheet:
  //   F=ABD'+B'C'D+BCD
endmodule
