// Logisim project örnek4.circ as structural Verilog: 1 circuit, main circuit main
module main (
  input  A,
  input  B,
  input  C,
  input  D,
  input  A_2,
  input  B_2,
  input  C_2,
  input  D_2,
  output out_9,
  output out_10
);

  wire and_1_out, and_2_out, and_3_out, and_4_out, and_5_out, and_6_out, not_1_out, not_2_out, not_3_out,
       not_4_out, not_5_out, not_6_out, not_7_out;

  not not_1 (not_1_out, B_2);
  not not_2 (not_2_out, C_2);
  not not_3 (not_3_out, B);
  not not_4 (not_4_out, D);
  not not_5 (not_5_out, B_2);
  not not_6 (not_6_out, D_2);
  not not_7 (not_7_out, C);
  and and_1 (and_1_out, B, D);
  and and_2 (and_2_out, not_7_out, D);
  and and_3 (and_3_out, not_3_out, not_4_out);
  and and_4 (and_4_out, not_1_out, not_2_out, D_2);
  and and_5 (and_5_out, B_2, D_2);
  and and_6 (and_6_out, not_5_out, not_6_out);
  or or_1 (out_9, and_1_out, and_2_out, and_3_out);
  or or_2 (out_10, and_4_out, and_5_out, and_6_out);

  // Notes on the sheet:
  //   F=BD+C'D+B'D'
  //   F=B'C'D+BD+B'D'
endmodule
